# Fritzing sketch MP3 (saved by Fritzing 0.9.3b)

parts:
  kEYPAD_MATRICIAL_1 = KEYPAD 4x3
  DFRobot_DFPlayer_Mini1 = DFRobot DFPlayer Mini [part_number=DFR0299]
  Speaker_2 = SPEAKER [package=pcb_mount_speaker]
  Part1 = Arduino Nano (Rev3.0) (ICSP)
  DFRobot_DFPlayer_Mini2 = DFRobot DFPlayer Mini [part_number=DFR0299]
  Speaker_1 = SPEAKER [package=pcb_mount_speaker]
  5V-1A = Battery Holders [package=battcon_20mm]
  R1 = Resistor [tolerance=±5% resistance=1k package="2010 [SMD]"]  # not connected
  R2 = Resistor [tolerance=±5% resistance=1k package="2010 [SMD]"]  # not connected

nets:
  N1: kEYPAD_MATRICIAL_1.col1, Part1.D12/MISO
  N2: kEYPAD_MATRICIAL_1.arrow1, Part1.D7
  N3: kEYPAD_MATRICIAL_1.col2, Part1.D6
  N4: kEYPAD_MATRICIAL_1.arrow2, Part1.D5
  N5: kEYPAD_MATRICIAL_1.col3, Part1.D4
  N6: kEYPAD_MATRICIAL_1.arrow3, Part1.D3
  N7: kEYPAD_MATRICIAL_1.arrow4, Part1.D2
  VCC: DFRobot_DFPlayer_Mini1.VCC, DFRobot_DFPlayer_Mini2.VCC, 5V-1A.+
  N8: DFRobot_DFPlayer_Mini1.TX, Part1.D10
  N9: DFRobot_DFPlayer_Mini1.SPK_1, Speaker_2.+
  N10: DFRobot_DFPlayer_Mini1.GND-1, DFRobot_DFPlayer_Mini1.GND-2, Part1.GND
  N11: DFRobot_DFPlayer_Mini1.SPK_2, Speaker_2.-
  N12: Part1.D8, DFRobot_DFPlayer_Mini2.TX
  N13: DFRobot_DFPlayer_Mini2.SPK_1, Speaker_1.+
  N14: DFRobot_DFPlayer_Mini2.SPK_2, Speaker_1.-

custom parts:
  KEYPAD 4x3: KEYPAD matricial de 12 botones, 4 filas x 3 columnas
